# Fritzing sketch Untitled Sketch (saved by Fritzing 0.9.4)

parts:
  J1 = Basic Servo  # not connected
  Компонент1 = Arduino Nano (Rev3.0) (ICSP)
  Компонент2 = Bluetooth HC-05 Macho
  hc-sr1 = hc-sr04

nets:
  N1: Компонент1.D2, Компонент2.TXD
  N2: Компонент1.D3, Компонент2.RXD
  N3: Компонент1.A1, hc-sr1.Trig
  N4: Компонент1.A0, hc-sr1.Echo
